# Fritzing sketch diy-modules (saved by Fritzing 0.9.3b)

parts:
  U1 = ESP32S-HiLetgo [part_number=ESP32S-HiLetgo]
  Load_Cell1 = Load Cell - Red/white/black/green
  M1 = MT3608 Module
  M2 = TP4056 Module [part_number=HW-107]
  U2 = LIPO-1000mAh [package=lipo-1000]
  S1 = SPST Switch [package=switch-spdt-smd]
  Part1 = HX711 Weighing Sensor Module
  R1 = Resistor [tolerance=±5% resistance=1M package=THT]
  R2 = Resistor [tolerance=±5% resistance=330k package=THT]

nets:
  N1: U1.3.3, Part1.VCC
  GND: U1.GND, M1.pin4, Part1.GND
  N2: U1.VIN, M1.pin3
  N3: U1.GPIO4, R1.Pin_1, R2.Pin_0
  N4: U1.GPIO18, Part1.DO/RX
  N5: U1.GPIO19, Part1.CK/TX
  N6: Load_Cell1.wire1, Part1.E+
  N7: Load_Cell1.wire2, Part1.A-
  N8: Load_Cell1.wire3, Part1.E-
  N9: Load_Cell1.wire4, Part1.A+
  N10: M1.pin1, M2.OUT-#1
  N11: M1.pin2, S1.O
  N12: M2.BAT-, U2.-, R1.Pin_0
  N13: M2.BAT+, U2.+, R2.Pin_1
  N14: M2.OUT-#4, S1.P

custom parts:
  ESP32S-HiLetgo: HiLetgo ESP-WROOM-32 ESP32 ESP-32S Development Board 2.4GHz Dual-Mode WiFi + Bluetooth Dual Cores Microcontroller The ESP32 integrated with Antenna switches, RF Balun, power amplifiers, low-noise amplifiers, filters, and management modules, and the entire solution occupies the least area of PCB. 2.4 GHz Wi-Fi plus Bluetooth dual-mode chip, with TSMC Ultra-low power consumption 40nm technology,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
  Load Cell - Red/white/black/green: A rectangle load cell/weighting pressure Sensor with four wires - Red, white, black, green. Normally corresponding with E+, E-, A+, A- respectively.
  MT3608 Module: MT3608 Boost Converter Module Links: Aerosemi MT3608 2A Step Up Converter datasheet
  TP4056 Module: TP4056 Lithium Battery Charge Management Module Links: TP4056 website
